// Logisim project contador até 9.circ as structural Verilog: 1 circuit, main circuit main
module main (
  input  in_1
);

  wire and_1_out, clock_1_out, j_k_ff_1_q, j_k_ff_1_qn, j_k_ff_2_q, j_k_ff_2_qn, j_k_ff_3_q, j_k_ff_3_qn,
       j_k_ff_4_q, main_1_a_2, main_1_b_2, main_1_c_2, main_1_d_2, main_1_e, main_1_f, main_1_g;

  Clock clock_1 (.out(clock_1_out));
  J_K_Flip_Flop j_k_ff_1 (
    .J(in_1), .clk(clock_1_out), .K(in_1), .Q(j_k_ff_1_q), .Qn(j_k_ff_1_qn), .en(in_1), .reset(and_1_out));  // open: preset
  decodificador_7_seg_main main_1 (
    .A(j_k_ff_4_q), .B(j_k_ff_3_q), .C(j_k_ff_2_q), .D(j_k_ff_1_q), .a_2(main_1_a_2), .b_2(main_1_b_2),
    .c_2(main_1_c_2), .d_2(main_1_d_2), .e(main_1_e), .f(main_1_f), .g(main_1_g));
  and and_1 (and_1_out, j_k_ff_4_q, j_k_ff_2_q);
  _7_Segment_Display u_7_segment_display_1 (
    .g(main_1_g), .f(main_1_f), .a(main_1_a_2), .b(main_1_b_2), .e(main_1_e), .d(main_1_d_2), .c(main_1_c_2));  // open: dp
  J_K_Flip_Flop j_k_ff_2 (
    .J(in_1), .clk(j_k_ff_1_qn), .K(in_1), .Q(j_k_ff_2_q), .Qn(j_k_ff_2_qn), .en(in_1), .reset(and_1_out));  // open: preset
  J_K_Flip_Flop j_k_ff_3 (
    .J(in_1), .clk(j_k_ff_2_qn), .K(in_1), .Q(j_k_ff_3_q), .Qn(j_k_ff_3_qn), .en(in_1), .reset(and_1_out));  // open: preset
  J_K_Flip_Flop j_k_ff_4 (
    .J(in_1), .clk(j_k_ff_3_qn), .K(in_1), .Q(j_k_ff_4_q), .en(in_1), .reset(and_1_out));  // open: Qn, preset
endmodule
