// Logisim project decodificador 7 seg.circ as structural Verilog: 1 circuit, main circuit main
module main (
  input  A,
  input  B,
  input  C,
  input  D,
  output a_2,
  output b_2,
  output c_2,
  output d_2,
  output e,
  output f,
  output g
);

  wire and_1_out, and_2_out, and_3_out, and_4_out, and_5_out, and_6_out, and_7_out, and_8_out, and_9_out,
       and_10_out, xnor_1_out, xnor_2_out, xor_1_out;

  xnor xnor_1 (xnor_1_out, B, D);
  xnor xnor_2 (xnor_2_out, C, D);
  or or_1 (c_2, B, ~C, D);  // OR_Gate
  and and_1 (and_1_out, ~B, ~D);  // AND_Gate
  and and_2 (and_2_out, ~B, C);  // AND_Gate
  and and_3 (and_3_out, C, ~D);  // AND_Gate
  and and_4 (and_4_out, B, ~C, D);  // AND_Gate
  and and_5 (and_5_out, ~B, ~D);  // AND_Gate
  and and_6 (and_6_out, C, ~D);  // AND_Gate
  and and_7 (and_7_out, ~C, ~D);  // AND_Gate
  and and_8 (and_8_out, B, ~C);  // AND_Gate
  and and_9 (and_9_out, B, ~D);  // AND_Gate
  or or_2 (a_2, xnor_1_out, C, A);
  or or_3 (b_2, xnor_2_out, ~B);  // OR_Gate
  or or_4 (e, and_5_out, and_6_out);
  or or_5 (f, A, and_7_out, and_8_out, and_9_out);
  xor xor_1 (xor_1_out, B, C);
  and and_10 (and_10_out, C, ~D);  // AND_Gate
  or or_6 (d_2, A, and_1_out, and_2_out, and_3_out, and_4_out);
  or or_7 (g, xor_1_out, A, and_10_out);
endmodule
