// Logisim project multiplicador8bits.circ as structural Verilog: 1 circuit, main circuit main
module main (
  input  [7:0] in_1,
  input  [7:0] in_2,
  output [15:0] out_3
);

  wire adder_1_cout, adder_2_cout, adder_3_cout, adder_4_cout, adder_5_cout, adder_6_cout;
  wire [6:0] adder_1_out, adder_3_out, adder_4_out, adder_5_out, adder_6_out;
  wire [7:0] multiplexer_2_out, multiplexer_3_out, multiplexer_4_out, multiplexer_5_out, multiplexer_6_out,
       multiplexer_7_out, multiplexer_8_out;
  wire [7:1] adder_2_out, multiplexer_1_out;

  Multiplexer #(.width(8)) multiplexer_1 (
    .in0({8{1'b0}}), .in1(in_2), .out({multiplexer_1_out, out_3[0]}), .sel(in_1[0]));  // open: en
  Multiplexer #(.width(8)) multiplexer_2 (
    .in0({8{1'b0}}), .in1(in_2), .out(multiplexer_2_out), .sel(in_1[1]));  // open: en
  Multiplexer #(.width(8)) multiplexer_3 (
    .in0({8{1'b0}}), .in1(in_2), .out(multiplexer_3_out), .sel(in_1[2]));  // open: en
  Multiplexer #(.width(8)) multiplexer_4 (
    .in0({8{1'b0}}), .in1(in_2), .out(multiplexer_4_out), .sel(in_1[3]));  // open: en
  Multiplexer #(.width(8)) multiplexer_5 (
    .in0({8{1'b0}}), .in1(in_2), .out(multiplexer_5_out), .sel(in_1[4]));  // open: en
  Multiplexer #(.width(8)) multiplexer_6 (
    .in0({8{1'b0}}), .in1(in_2), .out(multiplexer_6_out), .sel(in_1[5]));  // open: en
  Multiplexer #(.width(8)) multiplexer_7 (
    .in0({8{1'b0}}), .in1(in_2), .out(multiplexer_7_out), .sel(in_1[6]));  // open: en
  Multiplexer #(.width(8)) multiplexer_8 (
    .in0({8{1'b0}}), .in1(in_2), .out(multiplexer_8_out), .sel(in_1[7]));  // open: en
  Adder adder_1 (
    .a({1'b0, multiplexer_1_out}), .b(multiplexer_2_out), .out({adder_1_out, out_3[1]}), .cout(adder_1_cout));  // open: cin
  Adder adder_2 (
    .a({1'b0, adder_1_out}), .b(multiplexer_3_out), .out({adder_2_out, out_3[2]}), .cin(adder_1_cout),
    .cout(adder_2_cout));
  Adder adder_3 (
    .a({1'b0, adder_2_out}), .b(multiplexer_4_out), .out({adder_3_out, out_3[3]}), .cin(adder_2_cout),
    .cout(adder_3_cout));
  Adder adder_4 (
    .a({1'b0, adder_3_out}), .b(multiplexer_5_out), .out({adder_4_out, out_3[4]}), .cin(adder_3_cout),
    .cout(adder_4_cout));
  Adder adder_5 (
    .a({1'b0, adder_4_out}), .b(multiplexer_6_out), .out({adder_5_out, out_3[5]}), .cin(adder_4_cout),
    .cout(adder_5_cout));
  Adder adder_6 (
    .a({1'b0, adder_5_out}), .b(multiplexer_7_out), .out({adder_6_out, out_3[6]}), .cin(adder_5_cout),
    .cout(adder_6_cout));
  Adder adder_7 (
    .a({1'b0, adder_6_out}), .b(multiplexer_8_out), .out(out_3[14:7]), .cin(adder_6_cout), .cout(out_3[15]));
endmodule
