// Logisim project relogio.circ as structural Verilog: 6 circuits, main circuit main
module main (
);

  wire _0_5_2_out_3, _0_5_out_3, _0_9_2_out_3, _0_9_3_out_2, _0_9_out_3;
  wire [3:0] _0_2_out_2, _0_5_2_out_2, _0_5_out_2, _0_9_2_out_2, _0_9_3_out_1, _0_9_out_2;
  wire [6:0] controla_led_2_out_2, controla_led_3_out_2, controla_led_4_out_2, controla_led_5_out_2,
       controla_led_6_out_2, controla_led_out_2;

  _7_Segment_Display u_7_segment_display_1 (
    .g(controla_led_out_2[6]), .f(controla_led_out_2[3]), .a(controla_led_out_2[4]),
    .b(controla_led_out_2[5]), .e(controla_led_out_2[2]), .d(controla_led_out_2[1]), .c(controla_led_out_2[0]));  // open: dp
  Contador_LED controla_led (.out_2(controla_led_out_2), .in_1(_0_2_out_2));
  contador_0_2 _0_2 (.out_2(_0_2_out_2), .in_1(_0_9_out_3));  // open: out_3
  _7_Segment_Display u_7_segment_display_2 (
    .g(controla_led_2_out_2[6]), .f(controla_led_2_out_2[3]), .a(controla_led_2_out_2[4]),
    .b(controla_led_2_out_2[5]), .e(controla_led_2_out_2[2]), .d(controla_led_2_out_2[1]),
    .c(controla_led_2_out_2[0]));  // open: dp
  Contador_LED controla_led_2 (.out_2(controla_led_2_out_2), .in_1(_0_9_out_2));
  contador_0_9_com_entrada _0_9 (.out_2(_0_9_out_2), .in_1(_0_5_out_3), .out_3(_0_9_out_3));
  _7_Segment_Display u_7_segment_display_3 (
    .g(controla_led_3_out_2[6]), .f(controla_led_3_out_2[3]), .a(controla_led_3_out_2[4]),
    .b(controla_led_3_out_2[5]), .e(controla_led_3_out_2[2]), .d(controla_led_3_out_2[1]),
    .c(controla_led_3_out_2[0]));  // open: dp
  Contador_LED controla_led_3 (.out_2(controla_led_3_out_2), .in_1(_0_5_out_2));
  contador_0_5 _0_5 (.out_2(_0_5_out_2), .in_1(_0_9_2_out_3), .out_3(_0_5_out_3));
  _7_Segment_Display u_7_segment_display_4 (
    .g(controla_led_4_out_2[6]), .f(controla_led_4_out_2[3]), .a(controla_led_4_out_2[4]),
    .b(controla_led_4_out_2[5]), .e(controla_led_4_out_2[2]), .d(controla_led_4_out_2[1]),
    .c(controla_led_4_out_2[0]));  // open: dp
  Contador_LED controla_led_4 (.out_2(controla_led_4_out_2), .in_1(_0_9_2_out_2));
  contador_0_9_com_entrada _0_9_2 (.out_2(_0_9_2_out_2), .in_1(_0_5_2_out_3), .out_3(_0_9_2_out_3));
  _7_Segment_Display u_7_segment_display_5 (
    .g(controla_led_5_out_2[6]), .f(controla_led_5_out_2[3]), .a(controla_led_5_out_2[4]),
    .b(controla_led_5_out_2[5]), .e(controla_led_5_out_2[2]), .d(controla_led_5_out_2[1]),
    .c(controla_led_5_out_2[0]));  // open: dp
  Contador_LED controla_led_5 (.out_2(controla_led_5_out_2), .in_1(_0_5_2_out_2));
  contador_0_5 _0_5_2 (.out_2(_0_5_2_out_2), .in_1(_0_9_3_out_2), .out_3(_0_5_2_out_3));
  _7_Segment_Display u_7_segment_display_6 (
    .g(controla_led_6_out_2[6]), .f(controla_led_6_out_2[3]), .a(controla_led_6_out_2[4]),
    .b(controla_led_6_out_2[5]), .e(controla_led_6_out_2[2]), .d(controla_led_6_out_2[1]),
    .c(controla_led_6_out_2[0]));  // open: dp
  Contador_LED controla_led_6 (.out_2(controla_led_6_out_2), .in_1(_0_9_3_out_1));
  Contador_0_9 _0_9_3 (.out_1(_0_9_3_out_1), .out_2(_0_9_3_out_2));
endmodule

module Contador_0_9 (
  output [3:0] out_1,
  output out_2
);

  wire and_2_out, clock_1_out, not_1_out, not_2_out, not_3_out, not_4_out;

  T_Flip_Flop #(.trigger("falling")) t_ff_1 (
    .clk(out_1[2]), .T(1'b1), .Q(out_1[3]), .reset(and_2_out));  // open: Qn, preset, en
  T_Flip_Flop #(.trigger("falling")) t_ff_2 (
    .clk(out_1[1]), .T(1'b1), .Q(out_1[2]), .reset(and_2_out));  // open: Qn, preset, en
  T_Flip_Flop #(.trigger("falling")) t_ff_3 (
    .clk(out_1[0]), .T(1'b1), .Q(out_1[1]), .reset(and_2_out));  // open: Qn, preset, en
  Clock clock_1 (.out(clock_1_out));
  and and_1 (out_2, out_1[3], not_2_out, not_1_out, out_1[0]);
  not not_1 (not_1_out, out_1[1]);
  not not_2 (not_2_out, out_1[2]);
  T_Flip_Flop #(.trigger("falling")) t_ff_4 (
    .clk(clock_1_out), .T(1'b1), .Q(out_1[0]), .reset(and_2_out));  // open: Qn, preset, en
  not not_3 (not_3_out, out_1[2]);
  not not_4 (not_4_out, out_1[0]);
  and and_2 (and_2_out, out_1[3], not_3_out, out_1[1], not_4_out);
endmodule

module contador_0_5 (
  input  in_1,
  output [3:0] out_2,
  output out_3
);

  wire not_1_out, not_2_out;

  T_Flip_Flop #(.trigger("falling")) t_ff_1 (
    .clk(out_2[2]), .T(1'b1), .Q(out_2[3]), .reset(out_3));  // open: Qn, preset, en
  T_Flip_Flop #(.trigger("falling")) t_ff_2 (
    .clk(out_2[1]), .T(1'b1), .Q(out_2[2]), .reset(out_3));  // open: Qn, preset, en
  T_Flip_Flop #(.trigger("falling")) t_ff_3 (
    .clk(out_2[0]), .T(1'b1), .Q(out_2[1]), .reset(out_3));  // open: Qn, preset, en
  T_Flip_Flop #(.trigger("falling")) t_ff_4 (
    .clk(in_1), .T(1'b1), .Q(out_2[0]), .reset(out_3));  // open: Qn, preset, en
  not not_1 (not_1_out, out_2[3]);
  not not_2 (not_2_out, out_2[0]);
  and and_1 (out_3, not_1_out, out_2[2], out_2[1], not_2_out);
endmodule

module contador_0_2 (
  input  in_1,
  output [3:0] out_2,
  output out_3
);

  wire not_1_out, not_2_out;

  T_Flip_Flop #(.trigger("falling")) t_ff_1 (
    .clk(out_2[2]), .T(1'b1), .Q(out_2[3]), .reset(out_3));  // open: Qn, preset, en
  T_Flip_Flop #(.trigger("falling")) t_ff_2 (
    .clk(out_2[1]), .T(1'b1), .Q(out_2[2]), .reset(out_3));  // open: Qn, preset, en
  T_Flip_Flop #(.trigger("falling")) t_ff_3 (
    .clk(out_2[0]), .T(1'b1), .Q(out_2[1]), .reset(out_3));  // open: Qn, preset, en
  T_Flip_Flop #(.trigger("falling")) t_ff_4 (
    .clk(in_1), .T(1'b1), .Q(out_2[0]), .reset(out_3));  // open: Qn, preset, en
  not not_1 (not_1_out, out_2[3]);
  and and_1 (out_3, not_1_out, not_2_out, out_2[1], out_2[0]);
  not not_2 (not_2_out, out_2[2]);
endmodule

module Contador_LED (
  input  [3:0] in_1,
  output [6:0] out_2
);

  wire and_5_out, and_6_out, and_7_out, and_8_out, not_1_out, not_2_out, not_3_out, not_4_out, not_5_out,
       not_6_out, not_7_out, not_8_out, not_9_out, not_10_out, not_11_out, not_12_out, not_13_out,
       not_14_out, not_15_out, not_16_out, not_17_out, not_18_out, not_19_out, not_20_out, not_21_out,
       not_22_out, not_23_out, not_24_out, not_25_out, not_26_out, not_27_out, not_28_out, not_29_out,
       not_30_out, not_31_out, not_32_out, not_33_out, not_34_out, not_35_out, or_1_out, or_2_out, or_3_out,
       or_4_out, or_5_out, or_6_out, or_7_out, or_8_out, or_9_out, or_10_out, or_11_out, or_13_out,
       or_14_out, or_15_out;

  or or_1 (or_1_out, in_1[3], not_1_out, not_2_out, not_3_out);
  not not_1 (not_1_out, in_1[2]);
  not not_2 (not_2_out, in_1[1]);
  not not_3 (not_3_out, in_1[0]);
  and and_1 (out_2[6], or_1_out, or_3_out, or_2_out);
  or or_2 (or_2_out, in_1[3], in_1[2], in_1[1], in_1[0]);
  or or_3 (or_3_out, in_1[3], in_1[2], in_1[1], not_4_out);
  not not_4 (not_4_out, in_1[0]);
  or or_4 (or_4_out, in_1[3], not_6_out, not_5_out, in_1[0]);
  not not_5 (not_5_out, in_1[1]);
  not not_6 (not_6_out, in_1[2]);
  and and_2 (out_2[5], or_4_out, or_5_out);
  or or_5 (or_5_out, in_1[3], not_7_out, in_1[1], not_8_out);
  not not_7 (not_7_out, in_1[2]);
  not not_8 (not_8_out, in_1[0]);
  and and_3 (out_2[4], or_6_out, or_8_out);
  or or_6 (or_6_out, in_1[3], not_9_out, in_1[1], in_1[0]);
  not not_9 (not_9_out, in_1[2]);
  or or_7 (or_7_out, in_1[3], not_13_out, not_12_out, not_11_out);
  or or_8 (or_8_out, in_1[3], in_1[2], in_1[1], not_10_out);
  not not_10 (not_10_out, in_1[0]);
  not not_11 (not_11_out, in_1[0]);
  not not_12 (not_12_out, in_1[1]);
  not not_13 (not_13_out, in_1[2]);
  and and_4 (out_2[3], or_7_out, or_9_out, or_10_out, or_11_out);
  or or_9 (or_9_out, in_1[3], in_1[2], not_15_out, not_14_out);
  not not_14 (not_14_out, in_1[0]);
  not not_15 (not_15_out, in_1[1]);
  or or_10 (or_10_out, in_1[3], in_1[2], not_16_out, in_1[0]);
  not not_16 (not_16_out, in_1[1]);
  or or_11 (or_11_out, in_1[3], in_1[2], in_1[1], not_19_out);
  and and_5 (and_5_out, in_1[3], not_17_out, not_18_out, not_22_out);
  not not_17 (not_17_out, in_1[2]);
  not not_18 (not_18_out, in_1[1]);
  not not_19 (not_19_out, in_1[0]);
  and and_6 (and_6_out, not_20_out, in_1[2], in_1[1], not_21_out);
  not not_20 (not_20_out, in_1[3]);
  not not_21 (not_21_out, in_1[0]);
  not not_22 (not_22_out, in_1[0]);
  or or_12 (out_2[2], and_5_out, and_6_out, and_7_out, and_8_out);
  and and_7 (and_7_out, not_24_out, not_25_out, in_1[1], not_23_out);
  not not_23 (not_23_out, in_1[0]);
  not not_24 (not_24_out, in_1[3]);
  not not_25 (not_25_out, in_1[2]);
  and and_8 (and_8_out, not_26_out, not_29_out, not_27_out, not_28_out);
  not not_26 (not_26_out, in_1[3]);
  not not_27 (not_27_out, in_1[1]);
  not not_28 (not_28_out, in_1[0]);
  not not_29 (not_29_out, in_1[2]);
  or or_13 (or_13_out, in_1[3], not_32_out, not_30_out, not_31_out);
  not not_30 (not_30_out, in_1[1]);
  not not_31 (not_31_out, in_1[0]);
  not not_32 (not_32_out, in_1[2]);
  and and_9 (out_2[1], or_13_out, or_14_out, or_15_out);
  or or_14 (or_14_out, in_1[3], not_33_out, in_1[1], in_1[0]);
  not not_33 (not_33_out, in_1[2]);
  or or_15 (or_15_out, in_1[3], in_1[2], in_1[1], not_34_out);
  not not_34 (not_34_out, in_1[0]);
  or or_16 (out_2[0], in_1[3], in_1[2], not_35_out, in_1[0]);
  not not_35 (not_35_out, in_1[1]);
endmodule

module contador_0_9_com_entrada (
  input  in_1,
  output [3:0] out_2,
  output out_3
);

  wire not_1_out, not_2_out;

  T_Flip_Flop #(.trigger("falling")) t_ff_1 (
    .clk(out_2[2]), .T(1'b1), .Q(out_2[3]), .reset(out_3));  // open: Qn, preset, en
  T_Flip_Flop #(.trigger("falling")) t_ff_2 (
    .clk(out_2[1]), .T(1'b1), .Q(out_2[2]), .reset(out_3));  // open: Qn, preset, en
  T_Flip_Flop #(.trigger("falling")) t_ff_3 (
    .clk(out_2[0]), .T(1'b1), .Q(out_2[1]), .reset(out_3));  // open: Qn, preset, en
  T_Flip_Flop #(.trigger("falling")) t_ff_4 (
    .clk(in_1), .T(1'b1), .Q(out_2[0]), .reset(out_3));  // open: Qn, preset, en
  not not_1 (not_1_out, out_2[2]);
  and and_1 (out_3, out_2[3], not_1_out, out_2[1], not_2_out);
  not not_2 (not_2_out, out_2[0]);
endmodule
